# Fritzing sketch vectron_vr (saved by Fritzing 0.9.3b)
breadboards: 4

parts:
  U5 = IC, DIP package, 14 pins [chip_label=7404]
  U4 = IC, DIP package, 14 pins [chip_label=74HCT32]
  U3 = IC, DIP package, 20 pins [chip_label=74HCT688E]
  U2 = IC, DIP package, 16 pins [chip_label=74LS161A]
  U1 = IC, DIP package, 20 pins [chip_label=74ALS244AN]
  U6 = IC, DIP package, 20 pins [chip_label=74ALS244AN]
  U7 = IC, DIP package, 14 pins [chip_label=7404]
  U8 = IC, DIP package, 16 pins [chip_label=74165N]
  U9 = IC, DIP package, 14 pins [chip_label=7474]
  U10 = IC, DIP package, 14 pins [chip_label=7474]
  U11 = IC, DIP package, 14 pins [chip_label=7402]
  U12 = IC, DIP package, 14 pins [chip_label=74HCT32]
  U13 = IC, DIP package, 20 pins [chip_label=74HCT688E]  # not connected
  U14 = IC, DIP package, 20 pins [chip_label=74HCT688E]
  U15 = IC, DIP package, 20 pins [chip_label=74HCT688E]
  U16 = IC, DIP package, 20 pins [chip_label=74HCT688E]
  U17 = IC, DIP package, 20 pins [chip_label=74HCT688E]
  U18 = IC, DIP package, 20 pins [chip_label=74HCT688E]
  U19 = IC, DIP package, 20 pins [chip_label=74ALS244AN]
  U20 = IC, DIP package, 20 pins [chip_label=74ALS244AN]
  U21 = IC, DIP package, 20 pins [chip_label=74HCT688E]
  U22 = IC, DIP package, 20 pins [chip_label=74HCT688E]
  R1 = Resistor [tolerance=±5% resistance=220 package=THT]
  Q1 = TRANSISTOR_NPN [package=to-92-ammo]
  R2 = Resistor [tolerance=±5% resistance=220 package=THT]

nets:
  N1: U5.pin1, R1.Pin_0
  N2: U5.pin2, U2.pin2, U8.pin2
  N3: U5.pin4, U4.pin5
  N4: U5.pin5, U2.pin1, U7.pin4
  N5: U5.pin6, U4.pin4
  N6: U4.pin6, U1.pin1
  N7: U3.pin1, U3.pin2, U3.pin3, U3.pin4, U3.pin5, U3.pin6, U3.pin7, U3.pin8, U3.pin9, U3.pin10, U2.pin8, U1.pin10, U6.pin1, U6.pin10, U6.pin19, U7.pin7, U8.pin15, U9.pin7, U10.pin7, U11.pin7, U12.pin7, U19.pin1, U19.pin10, U19.pin19, U20.pin1, U20.pin10, U20.pin19, Q1.E
  N8: U2.pin7, U6.pin20, U7.pin14, U8.pin16, U9.pin1, U9.pin4, U9.pin14, U10.pin1, U10.pin4, U11.pin14, U12.pin14, U19.pin20, U20.pin20, R1.Pin_1
  N9: U1.pin3, Q1.C
  N10: U6.pin3, U8.pin6
  N11: U6.pin5, U8.pin5
  N12: U6.pin7, U8.pin4
  N13: U6.pin9, U8.pin3
  N14: U6.pin12, U8.pin14
  N15: U6.pin14, U8.pin13
  N16: U6.pin16, U8.pin12
  N17: U6.pin18, U8.pin11, U9.pin2, U10.pin2, U10.pin12
  N18: U7.pin3, U11.pin1
  N19: U7.pin5, U12.pin3
  N20: U7.pin6, U9.pin3
  N21: U8.pin1, U12.pin11
  N22: U10.pin3, U11.pin13
  N23: U10.pin11, U11.pin10
  N24: U11.pin2, U18.pin19
  N25: U11.pin3, U11.pin5, U11.pin8, U11.pin11, U12.pin1, U12.pin6, U12.pin13
  N26: U11.pin4, R2.Pin_0
  N27: U11.pin6, U17.pin19
  N28: U11.pin9, U22.pin19
  N29: U11.pin12, U16.pin19
  N30: U12.pin2, U15.pin19
  N31: U12.pin4, U21.pin19
  N32: U12.pin12, U14.pin19
  N33: Q1.B, R2.Pin_1

notes:
  To 7MHz Oscillator
  To 5V DC
  To Vectron 64 Data Bus:
  0
  1
  2
  3
  To Vectron 64 Data Bus:
  4
  5
  6
  7
  To 6502 PHI1O
  To Vectron 64 Address Bus:
  0
  1
  2
  3
  To Vectron 64 Address Bus:
  4
  5
  6
  7
  To Vectron 64 Address Bus:
  8
  9
  10
  11
  To Vectron 64 Address Bus:
  12
  13
  14
  15
